# Fritzing sketch SCF_perfboard (saved by Fritzing 0.9.3b)
perfboards: 2

parts:
  R1 = Resistor [tolerance=±5% resistance=10k package="1206 [SMD]"]
  R2 = Resistor [tolerance=±5% resistance=10k package="1206 [SMD]"]
  R3 = Resistor [tolerance=±5% resistance=10k package="1206 [SMD]"]
  D1 = Diode [package=diode-1n4148]
  J24 = single row smd female pin header, 4 pins [form="♀ (female)"]
  J25 = single row smd female pin header, 5 pins [form="♀ (female)"]
  J26 = female pin header, 5 pins [form="♀ (female)"]
  IC4 = ULN2003A [package="SO16 [SMD]"]
  C3 = Capacitor [package=cap-pth-small2]
  C4 = Capacitor [package=cap-pth-small2]
  IC5 = ULN2003A [package="SO16 [SMD]"]
  R7 = Resistor [tolerance=±5% resistance=10k package="1206 [SMD]"]
  R8 = Resistor [tolerance=±5% resistance=10k package="1206 [SMD]"]
  R9 = Resistor [tolerance=±5% resistance=10k package="1206 [SMD]"]
  D3 = Diode [package=diode-1n4148]
  J27 = single row smd female pin header, 2 pins [form="♀ (female)"]
  J28 = single row smd female pin header, 5 pins [form="♀ (female)"]
  J29 = single row smd female pin header, 2 pins [form="♀ (female)"]
  J30 = single row smd female pin header, 4 pins [form="♀ (female)"]
  J31 = female pin header, 5 pins [form="♀ (female)"]
  J32 = single row smd female pin header, 2 pins [form="♀ (female)"]

nets:
  N1: R1.Pin_1, R2.Pin_1
  N2: R3.Pin_1, J26.pin5
  N3: D1.A, J26.pin1
  N4: J24.pin1, IC4.0V, C3.2
  N5: J24.pin2, IC4.COM_-_Common, C3.1
  N6: J24.pin3, J32.pin2
  N7: J24.pin4, IC4.In_4
  N8: J25.pin2, IC4.Out_1
  N9: J25.pin3, IC4.Out_2
  N10: J25.pin4, IC4.Out_3
  N11: J25.pin5, IC4.Out_4
  N12: J26.pin2, IC4.In_3
  N13: J26.pin3, IC4.In_2
  N14: J26.pin4, IC4.In_1
  N15: C4.1, IC5.0V, J29.pin1, J30.pin1
  N16: C4.2, IC5.COM_-_Common, J30.pin2
  N17: IC5.In_1, J31.pin4
  N18: IC5.In_2, J31.pin3
  N19: IC5.In_3, J31.pin2
  N20: IC5.In_4, J30.pin4
  N21: IC5.Out_4, J28.pin5
  N22: IC5.Out_3, J28.pin4
  N23: IC5.Out_2, J28.pin3
  N24: IC5.Out_1, J28.pin2
  N25: R7.Pin_1, J31.pin5
  N26: R8.Pin_0, J27.pin2
  N27: R8.Pin_1, R9.Pin_1, D3.C
  N28: R9.Pin_0, J27.pin1
  N29: J29.pin2, J30.pin3

notes:
  3v3 G22 G19 G23 G33
  G21 G25 5V GND
  catflap out
  homeswitch
  28BYJ
